// Logisim project alu.circ as structural Verilog: 11 circuits, main circuit main
module main (
  input  [31:0] X,
  input  [31:0] Y,
  input  [3:0] Switch,
  output Signed_Overflow,
  output Equal,
  output [31:0] Result
);

  wire OFadd, OFsub;
  wire [31:0] ADD_5_out, ADDU_6_out, AND_9_out, OR_10_out, SLL_0_out, SLT_11_out, SLTU_12_out, SRA_2_out,
       SRL_1_out, SUB_7_out, SUBU_8_out, undriven, undriven_2, undriven_3, undriven_4, undriven_5;

  SLL_0 SLL_0 (.Y(Y), .X(X), .out(SLL_0_out));
  SRL_1 SRL_1 (.Y(Y), .X(X), .out(SRL_1_out));
  SRA_2 SRA_2 (.Y(Y), .X(X), .out(SRA_2_out));
  add_5 ADD_5 (.X(X), .Y(Y), .out(ADD_5_out), .out_2(OFadd));
  addu_6 ADDU_6 (.X(X), .Y(Y), .out(ADDU_6_out));
  sub_7 SUB_7 (.X(X), .Y(Y), .out(SUB_7_out), .out_2(OFsub));
  subu_8 SUBU_8 (.X(X), .Y(Y), .out(SUBU_8_out));
  assign AND_9_out = X & Y;  // AND_Gate AND_9, 32 bits wide
  assign OR_10_out = X | Y;  // OR_Gate OR_10, 32 bits wide
  slt_11 SLT_11 (.X(X), .Y(Y), .out(SLT_11_out));
  sltu_12 SLTU_12 (.X(X), .Y(Y), .out(SLTU_12_out));
  Comparator #(.width(32)) comparator_1 (.a(Y), .b(X), .eq(Equal));  // open: gt, lt
  Multiplexer #(.select(4), .width(32)) multiplexer_1 (
    .in0(SLL_0_out), .in1(SRL_1_out), .in2(SRA_2_out), .in3(undriven), .in4(undriven_2), .in5(ADD_5_out),
    .in6(ADDU_6_out), .in7(SUB_7_out), .in8(SUBU_8_out), .in9(AND_9_out), .in10(OR_10_out),
    .in11(SLT_11_out), .in12(SLTU_12_out), .in13(undriven_3), .in14(undriven_4), .in15(undriven_5),
    .out(Result), .sel(Switch));  // open: en
  Multiplexer #(.select(4)) multiplexer_2 (
    .in0(1'b0), .in1(1'b0), .in2(1'b0), .in3(1'b0), .in4(1'b0), .in5(OFadd), .in6(1'b0), .in7(OFsub),
    .in8(1'b0), .in9(1'b0), .in10(1'b0), .in11(1'b0), .in12(1'b0), .in13(1'b0), .in14(1'b0), .in15(1'b0),
    .out(Signed_Overflow), .sel(Switch));  // open: en

  // Other names for the same wires on the sheet: overflow = Signed_Overflow; S[3:0] = Switch

  // Notes on the sheet:
  //   INPUTS to your circuit
  //   DON'T CHANGE THE LOCATIONS OF THE INPUTS AND OUTPUTS!
  //   OUTPUTS from your circuit
endmodule

module SLL_0 (
  input  [31:0] Y,
  input  [31:0] X,
  output [31:0] out
);

  Shifter #(.width(32)) shifter_1 (.in(Y), .\dist (X[4:0]), .out(out));
endmodule

module SRL_1 (
  input  [31:0] Y,
  input  [31:0] X,
  output [31:0] out
);

  Shifter #(.width(32), .shift("lr")) shifter_1 (.in(Y), .\dist (X[4:0]), .out(out));
endmodule

module SRA_2 (
  input  [31:0] Y,
  input  [31:0] X,
  output [31:0] out
);

  Shifter #(.width(32), .shift("ar")) shifter_1 (.in(Y), .\dist (X[4:0]), .out(out));
endmodule

module add_5 (
  input  [31:0] X,
  input  [31:0] Y,
  output [31:0] out,
  output out_2
);

  wire adder_1_cout, adder_2_cout;

  Adder #(.width(31)) adder_1 (.a(X[30:0]), .b(Y[30:0]), .cout(adder_1_cout));  // open: out, cin
  Adder #(.width(32)) adder_2 (.a(X), .b(Y), .out(out), .cout(adder_2_cout));  // open: cin
  xor xor_1 (out_2, adder_2_cout, adder_1_cout);
endmodule

module addu_6 (
  input  [31:0] X,
  input  [31:0] Y,
  output [31:0] out
);

  Adder #(.width(32)) adder_1 (.a(X), .b(Y), .out(out));  // open: cin, cout
endmodule

module sub_7 (
  input  [31:0] X,
  input  [31:0] Y,
  output [31:0] out,
  output out_2
);

  wire adder_1_cout, adder_2_cout;
  wire [31:0] not_1_out;

  assign not_1_out = ~Y;  // NOT_Gate not_1, 32 bits wide
  Adder #(.width(32)) adder_1 (.a(X), .b(not_1_out), .out(out), .cin(1'b1), .cout(adder_1_cout));
  Adder #(.width(31)) adder_2 (.a(X[30:0]), .b(not_1_out[30:0]), .cin(1'b1), .cout(adder_2_cout));  // open: out
  xor xor_1 (out_2, adder_1_cout, adder_2_cout);
endmodule

module subu_8 (
  input  [31:0] X,
  input  [31:0] Y,
  output [31:0] out
);

  Subtractor #(.width(32)) subtractor_1 (.a(X), .b(Y), .out(out));  // open: bin, bout
endmodule

module slt_11 (
  input  [31:0] X,
  input  [31:0] Y,
  output [31:0] out
);

  Comparator #(.width(32)) comparator_1 (.a(X), .b(Y), .lt(out[0]));  // open: gt, eq

  assign out[31:1] = {31{1'b0}};
endmodule

module sltu_12 (
  input  [31:0] X,
  input  [31:0] Y,
  output [31:0] out
);

  Comparator #(.width(32), .mode("unsigned")) comparator_1 (.a(X), .b(Y), .lt(out[0]));  // open: gt, eq

  assign out[31:1] = {31{1'b0}};
endmodule

module compareSelect (
  input  OF,
  input  [3:0] switch,
  input  [3:0] code,
  output out
);

  wire comparator_1_eq;

  Comparator #(.width(4)) comparator_1 (.a(switch), .b(code), .eq(comparator_1_eq));  // open: gt, lt
  and and_1 (out, OF, comparator_1_eq);
endmodule
