// Logisim project cpu.circ as structural Verilog: 4 circuits, main circuit main
module main (
  input  [31:0] INSTRUCTION,
  input  CLOCK,
  output [31:0] FETCH_ADDRESS,
  output [31:0] s0_Value,
  output [31:0] s1_Value,
  output [31:0] s2_Value,
  output [31:0] ra_Value,
  output [31:0] sp_Value,
  output equal
);

  wire ALUSrc, and_1_out, and_2_out, beq, bne, comparator_1_eq, comparator_2_eq, comparator_3_eq,
       comparator_6_eq, comparator_7_eq, comparator_8_eq, Ext_Op, j_jal_jr, jump, main_2_signed_overflow,
       MemtoReg, MemWr, not_1_out, nPC_sel_Equal, or_1_out, RegDst, RegWr, shift;
  wire [3:0] ALUCtr;
  wire [4:0] multiplexer_4_out, rd, rs, rt, shampt;
  wire [5:0] funct, opcode;
  wire [15:0] imm;
  wire [25:0] adr, shifter_1_out;
  wire [27:0] bit_extender_2_out;
  wire [31:0] adder_1_out, adder_2_out, bit_extender_1_out, main_1_read_data_1, main_1_read_data_2,
       main_2_result, main_3_p5, multiplexer_1_out, multiplexer_2_out, multiplexer_3_out, multiplexer_5_out,
       multiplexer_6_out, multiplexer_7_out, register_1_q, shamt, shifter_2_out, SignedExt_imm32bit;

  assign bit_extender_1_out = {{16{1'b0}}, imm};  // Bit_Extender bit_extender_1
  Shifter #(.width(26)) shifter_1 (.in(adr), .\dist (5'b00010), .out(shifter_1_out));
  Adder #(.width(32)) adder_1 (.a(32'h4), .b(FETCH_ADDRESS), .out(adder_1_out));  // open: cin, cout
  Shifter #(.width(32)) shifter_2 (.in(bit_extender_1_out), .\dist (5'b00010), .out(shifter_2_out));
  assign bit_extender_2_out = {{2{1'b0}}, shifter_1_out};  // Bit_Extender bit_extender_2
  Adder #(.width(32)) adder_2 (.a(adder_1_out), .b(shifter_2_out), .out(adder_2_out));  // open: cin, cout
  Multiplexer #(.width(32), .enable("false")) multiplexer_1 (
    .in0(adder_1_out), .in1(adder_2_out), .out(multiplexer_1_out), .sel(nPC_sel_Equal));
  or or_1 (or_1_out, j_jal_jr, nPC_sel_Equal);
  Multiplexer #(.width(32), .enable("false")) multiplexer_2 (
    .in0(multiplexer_1_out), .in1({adder_1_out[31:28], bit_extender_2_out}), .out(multiplexer_2_out),
    .sel(jump));
  Multiplexer #(.width(32), .enable("false")) multiplexer_3 (
    .in0(INSTRUCTION), .in1({32{1'b0}}), .out(multiplexer_3_out), .sel(or_1_out));
  // Probe on nothing
  Register #(.width(32)) PC (.D(multiplexer_2_out), .Q(FETCH_ADDRESS), .clk(CLOCK));  // open: en, clr
  Register #(.width(32)) register_1 (.D(multiplexer_3_out), .Q(register_1_q), .clk(CLOCK));  // open: en, clr
  // Probe on nothing
  decode decode_1 (
    .instruction(register_1_q), .funct(funct), .shampt(shampt), .rd(rd), .rt(rt), .rs(rs), .opcode(opcode),
    .immidiate(imm), .address(adr));
  Multiplexer #(.width(5), .enable("false")) multiplexer_4 (.in0(rt), .in1(rd), .out(multiplexer_4_out), .sel(RegDst));
  assign shamt = {{27{1'b0}}, shampt};  // Bit_Extender bit_extender_3
  regfile_main main_1 (
    .Read_Register_1(rs), .Read_Register_2(rt), .Write_Register(multiplexer_4_out),
    .Write_Data(multiplexer_7_out), .Write_Enable(RegWr), .Clock(CLOCK), .Read_Data_1(main_1_read_data_1),
    .Read_Data_2(main_1_read_data_2), .s0_Value(s0_Value), .s1_Value(s1_Value), .s2_Value(s2_Value),
    .ra_Value(ra_Value), .sp_Value(sp_Value));
  Control_Unit control_unit_1 (
    .RegDst(RegDst), .ALUctr(ALUCtr), .MemWr(MemWr), .MemtoReg(MemtoReg), .Ext_Op(Ext_Op), .opcode(opcode),
    .funct(funct), .RegWr(RegWr), .ALUSrc(ALUSrc));
  Multiplexer #(.width(32), .enable("false")) multiplexer_5 (
    .in0(main_1_read_data_2), .in1(SignedExt_imm32bit), .out(multiplexer_5_out), .sel(ALUSrc));
  SignedExt SignedExt (.imm(imm), .ExOP(Ext_Op), .imm32bit(SignedExt_imm32bit));
  Multiplexer #(.width(32), .enable("false")) multiplexer_6 (
    .in0(main_1_read_data_1), .in1(shamt), .out(multiplexer_6_out), .sel(shift));
  LED led_1 (.in(main_2_signed_overflow));
  alu_main main_2 (
    .Switch(ALUCtr), .X(multiplexer_6_out), .Equal(equal), .Result(main_2_result),
    .Signed_Overflow(main_2_signed_overflow), .Y(multiplexer_5_out));
  not not_1 (not_1_out, equal);
  and and_1 (and_1_out, beq, equal);
  and and_2 (and_2_out, bne, not_1_out);
  // mem_main main_3: pin names not known; wires that end beside it: main_2_result, main_1_read_data_2, MemWr, CLOCK, main_3_p5
  Comparator #(.width(6)) comparator_1 (.a(opcode), .b(6'b000011), .eq(comparator_1_eq));  // open: gt, lt
  Comparator #(.width(6)) comparator_2 (.a(opcode), .b(6'b000010), .eq(comparator_2_eq));  // open: gt, lt
  Comparator #(.width(6)) comparator_3 (.a(funct), .b(6'b001000), .eq(comparator_3_eq));  // open: gt, lt
  or or_2 (nPC_sel_Equal, and_1_out, and_2_out);
  Multiplexer #(.width(32), .enable("false")) multiplexer_7 (
    .in0(main_2_result), .in1(main_3_p5), .out(multiplexer_7_out), .sel(MemtoReg));
  or or_3 (jump, comparator_1_eq, comparator_2_eq);
  or or_4 (j_jal_jr, comparator_3_eq, jump);
  Comparator #(.width(6)) comparator_4 (.a(opcode), .b(6'b000100), .eq(beq));  // open: gt, lt
  Comparator #(.width(6)) comparator_5 (.a(opcode), .b(6'b000101), .eq(bne));  // open: gt, lt
  Comparator #(.width(6)) comparator_6 (.a(funct), .b({6{1'b0}}), .eq(comparator_6_eq));  // open: gt, lt
  Comparator #(.width(6)) comparator_7 (.a(funct), .b(6'b000010), .eq(comparator_7_eq));  // open: gt, lt
  Comparator #(.width(6)) comparator_8 (.a(funct), .b(6'b000011), .eq(comparator_8_eq));  // open: gt, lt
  or or_5 (shift, comparator_6_eq, comparator_7_eq, comparator_8_eq);

  // Other names for the same wires on the sheet: clk = CLOCK; fetch_addr[31:0] = FETCH_ADDRESS; ra[31:0] = ra_Value;
  //   s0[31:0] = s0_Value; s1[31:0] = s1_Value; s2[31:0] = s2_Value; sp[31:0] = sp_Value

  // Notes on the sheet:
  //   Output
  //   These are outputs/inputs from run.circ
  //   Inputs
  //   Pipelining 
  //   These are DEBUG/TEST outputs from your circuit.
  //   busW
  //   ALUControl
  //   jal
  //   j
  //   jr
  //   More control signals
  //   beq
  //   beq
  //   sll
  //   srl
  //   sra
endmodule

module decode (
  input  [31:0] instruction,
  output [5:0] funct,
  output [4:0] shampt,
  output [4:0] rd,
  output [4:0] rt,
  output [4:0] rs,
  output [5:0] opcode,
  output [15:0] immidiate,
  output [25:0] address
);


  assign address = instruction[25:0];
  assign funct = instruction[5:0];
  assign immidiate = instruction[15:0];
  assign opcode = instruction[31:26];
  assign rd = instruction[15:11];
  assign rs = instruction[25:21];
  assign rt = instruction[20:16];
  assign shampt = instruction[10:6];
endmodule

module SignedExt (
  input  ExOP,
  input  [15:0] imm,
  output [31:0] imm32bit
);

  assign imm32bit = {{16{imm[15]}}, imm};  // Bit_Extender bit_extender_1
endmodule

module Control_Unit (
  input  [5:0] opcode,
  input  [5:0] funct,
  output RegDst,
  output [3:0] ALUctr,
  output MemWr,
  output MemtoReg,
  output Ext_Op,
  output RegWr,
  output ALUSrc
);

  wire branch, comparator_2_eq, comparator_3_eq, comparator_4_eq, comparator_5_eq, comparator_6_eq,
       comparator_7_eq, comparator_8_eq, comparator_9_eq, comparator_11_eq, comparator_12_eq, jump,
       not_1_out, not_2_out, or_1_out, or_2_out;
  wire [3:0] multiplexer_1_out, multiplexer_2_out, undriven;

  Multiplexer #(.select(5), .width(4)) multiplexer_1 (
    .in4(4'b0110), .in5(4'b0110), .in8(4'b0101), .in9(4'b0110), .in10(4'b1011), .in11(4'b1100),
    .in12(4'b1001), .in13(4'b1010), .in15(4'b0110), .in19(4'b0101), .in27(4'b0110), .in28(4'b0110),
    .out(multiplexer_1_out), .sel({opcode[5], opcode[3:0]}));  // open: in0, in1, in2, in3, in6, in7, in14, in16, in17, in18, in20, in21, in22, in23, in24, in25, in26, in29, in30, in31, en
  Multiplexer #(.select(5), .width(4)) multiplexer_2 (
    .in0(4'b0000), .in2(4'b0001), .in3(4'b0010), .in8(undriven), .in16(4'b0101), .in17(4'b0110),
    .in18(4'b0111), .in19(4'b1000), .in20(4'b1001), .in21(4'b1010), .in26(4'b1011), .in27(4'b1100),
    .out(multiplexer_2_out), .sel({funct[5], funct[3:0]}));  // open: in1, in4, in5, in6, in7, in9, in10, in11, in12, in13, in14, in15, in22, in23, in24, in25, in28, in29, in30, in31, en
  Comparator #(.width(6)) comparator_1 (.a(opcode), .b({6{1'b0}}), .eq(RegDst));  // open: gt, lt
  Multiplexer #(.width(4), .enable("false")) multiplexer_3 (
    .in0(multiplexer_1_out), .in1(multiplexer_2_out), .out(ALUctr), .sel(RegDst));
  Comparator #(.width(6)) comparator_2 (.a(opcode), .b(6'b000101), .eq(comparator_2_eq));  // open: gt, lt
  Comparator #(.width(6)) comparator_3 (.a(opcode), .b(6'b000100), .eq(comparator_3_eq));  // open: gt, lt
  Comparator #(.width(6)) comparator_4 (.a(opcode), .b({6{1'b0}}), .eq(comparator_4_eq));  // open: gt, lt
  Comparator #(.width(6)) comparator_5 (.a(opcode), .b(6'b101011), .eq(comparator_5_eq));  // open: gt, lt
  Comparator #(.width(6)) comparator_6 (.a(opcode), .b(6'b101100), .eq(comparator_6_eq));  // open: gt, lt
  or or_1 (or_1_out, MemWr, jump, branch);
  not not_1 (not_1_out, comparator_4_eq);
  or or_2 (or_2_out, branch, jump);
  not not_2 (not_2_out, or_2_out);
  Comparator #(.width(6)) comparator_7 (.a(opcode), .b(6'b100011), .eq(comparator_7_eq));  // open: gt, lt
  Comparator #(.width(6)) comparator_8 (.a(opcode), .b(6'b101011), .eq(comparator_8_eq));  // open: gt, lt
  Comparator #(.width(6)) comparator_9 (.a(opcode), .b(6'b101100), .eq(comparator_9_eq));  // open: gt, lt
  Comparator #(.width(6)) comparator_10 (.a(opcode), .b(6'b100011), .eq(MemtoReg));  // open: gt, lt
  or or_3 (MemWr, comparator_5_eq, comparator_6_eq);
  or or_4 (branch, comparator_2_eq, comparator_3_eq);
  not not_3 (RegWr, or_1_out);
  and and_1 (ALUSrc, not_1_out, not_2_out);
  or or_5 (Ext_Op, comparator_7_eq, comparator_8_eq, comparator_9_eq);
  Comparator #(.width(6)) comparator_11 (.a(opcode), .b(6'b000011), .eq(comparator_11_eq));  // open: gt, lt
  Comparator #(.width(6)) comparator_12 (.a(opcode), .b(6'b000010), .eq(comparator_12_eq));  // open: gt, lt
  or or_6 (jump, comparator_11_eq, comparator_12_eq);

  // Other names for the same wires on the sheet: ExtOp = Ext_Op

  // Notes on the sheet:
  //   slti
  //   ori
  //   sub
  //   addiu
  //   sltiu
  //   sra
  //   addu
  //   subu
  //   or
  //   sltu
  //   addi
  //   andi
  //   lw
  //   sll
  //   srl
  //   add
  //   and
  //   slt
  //   swinc
  //   beq
  //   bne
  //   lw
  //   sw
  //   lw
  //   sw
  //   swinc
  //   jal
  //   j
endmodule
