// Logisim project regfile.circ as structural Verilog: 1 circuit, main circuit main
module main (
  input  [4:0] Read_Register_1,
  input  [4:0] Read_Register_2,
  input  [4:0] Write_Register,
  input  [31:0] Write_Data,
  input  Write_Enable,
  input  Clock,
  output [31:0] s0_Value,
  output [31:0] s1_Value,
  output [31:0] s2_Value,
  output [31:0] ra_Value,
  output [31:0] sp_Value,
  output [31:0] Read_Data_1,
  output [31:0] Read_Data_2
);

  wire demultiplexer_1_out0, demultiplexer_1_out1, demultiplexer_1_out2, demultiplexer_1_out3,
       demultiplexer_1_out4, demultiplexer_1_out5, demultiplexer_1_out6, demultiplexer_1_out7,
       demultiplexer_1_out8, demultiplexer_1_out9, demultiplexer_1_out10, demultiplexer_1_out11,
       demultiplexer_1_out12, demultiplexer_1_out13, demultiplexer_1_out14, demultiplexer_1_out15,
       demultiplexer_1_out16, demultiplexer_1_out17, demultiplexer_1_out18, demultiplexer_1_out19,
       demultiplexer_1_out20, demultiplexer_1_out21, demultiplexer_1_out22, demultiplexer_1_out23,
       demultiplexer_1_out24, demultiplexer_1_out25, demultiplexer_1_out26, demultiplexer_1_out27,
       demultiplexer_1_out28, demultiplexer_1_out29, demultiplexer_1_out30, demultiplexer_1_out31;
  wire [31:0] o1, o2, o3, o4, o5, o6, o7, o8, o9, o10, o11, o12, o13, o14, o15, o19, o20, o21, o22, o23, o24,
       o25, o26, o27, o28, o30;

  Demultiplexer #(.select(5)) demultiplexer_1 (
    .out0(demultiplexer_1_out0), .out1(demultiplexer_1_out1), .out2(demultiplexer_1_out2),
    .out3(demultiplexer_1_out3), .out4(demultiplexer_1_out4), .out5(demultiplexer_1_out5),
    .out6(demultiplexer_1_out6), .out7(demultiplexer_1_out7), .out8(demultiplexer_1_out8),
    .out9(demultiplexer_1_out9), .out10(demultiplexer_1_out10), .out11(demultiplexer_1_out11),
    .out12(demultiplexer_1_out12), .out13(demultiplexer_1_out13), .out14(demultiplexer_1_out14),
    .out15(demultiplexer_1_out15), .out16(demultiplexer_1_out16), .out17(demultiplexer_1_out17),
    .out18(demultiplexer_1_out18), .out19(demultiplexer_1_out19), .out20(demultiplexer_1_out20),
    .out21(demultiplexer_1_out21), .out22(demultiplexer_1_out22), .out23(demultiplexer_1_out23),
    .out24(demultiplexer_1_out24), .out25(demultiplexer_1_out25), .out26(demultiplexer_1_out26),
    .out27(demultiplexer_1_out27), .out28(demultiplexer_1_out28), .out29(demultiplexer_1_out29),
    .out30(demultiplexer_1_out30), .out31(demultiplexer_1_out31), .in(Write_Enable), .sel(Write_Register));  // open: en
  Register #(.width(32)) register_1 (.D(Write_Data), .en(demultiplexer_1_out2), .Q(o2), .clk(Clock));  // open: clr
  Register #(.width(32)) register_2 (.D(Write_Data), .en(demultiplexer_1_out4), .Q(o4), .clk(Clock));  // open: clr
  Register #(.width(32)) register_3 (.D(Write_Data), .en(demultiplexer_1_out6), .Q(o6), .clk(Clock));  // open: clr
  Register #(.width(32)) register_4 (.D(Write_Data), .en(demultiplexer_1_out8), .Q(o8), .clk(Clock));  // open: clr
  Register #(.width(32)) register_5 (.D(Write_Data), .en(demultiplexer_1_out10), .Q(o10), .clk(Clock));  // open: clr
  Register #(.width(32)) register_6 (.D(Write_Data), .en(demultiplexer_1_out22), .Q(o22), .clk(Clock));  // open: clr
  Register #(.width(32)) register_7 (.D(Write_Data), .en(demultiplexer_1_out24), .Q(o24), .clk(Clock));  // open: clr
  Register #(.width(32)) register_8 (.D(Write_Data), .en(demultiplexer_1_out26), .Q(o26), .clk(Clock));  // open: clr
  Register #(.width(32)) register_9 (.D(Write_Data), .Q(o28), .clk(Clock));  // open: en, clr
  Register #(.width(32)) register_10 (.D(Write_Data), .en(demultiplexer_1_out30), .Q(o30), .clk(Clock));  // open: clr
  Register #(.width(32)) register_11 (.D(Write_Data), .en(demultiplexer_1_out12), .Q(o12), .clk(Clock));  // open: clr
  Register #(.width(32)) register_12 (.D(Write_Data), .en(demultiplexer_1_out14), .Q(o14), .clk(Clock));  // open: clr
  Register #(.width(32)) register_13 (
    .D(Write_Data), .en(demultiplexer_1_out16), .Q(s0_Value), .clk(Clock));  // open: clr
  Register #(.width(32)) register_14 (
    .D(Write_Data), .en(demultiplexer_1_out18), .Q(s2_Value), .clk(Clock));  // open: clr
  Register #(.width(32)) register_15 (.D(Write_Data), .en(demultiplexer_1_out20), .Q(o20), .clk(Clock));  // open: clr
  Register #(.width(32)) register_16 (.D(Write_Data), .en(demultiplexer_1_out1), .Q(o1), .clk(Clock));  // open: clr
  Register #(.width(32)) register_17 (.D(Write_Data), .en(demultiplexer_1_out3), .Q(o3), .clk(Clock));  // open: clr
  Register #(.width(32)) register_18 (.D(Write_Data), .en(demultiplexer_1_out5), .Q(o5), .clk(Clock));  // open: clr
  Register #(.width(32)) register_19 (.D(Write_Data), .en(demultiplexer_1_out7), .Q(o7), .clk(Clock));  // open: clr
  Register #(.width(32)) register_20 (.D(Write_Data), .en(demultiplexer_1_out9), .Q(o9), .clk(Clock));  // open: clr
  Register #(.width(32)) register_21 (.D(Write_Data), .en(demultiplexer_1_out25), .Q(o25), .clk(Clock));  // open: clr
  Register #(.width(32)) register_22 (.D(Write_Data), .en(demultiplexer_1_out27), .Q(o27), .clk(Clock));  // open: clr
  Register #(.width(32)) register_23 (
    .D(Write_Data), .en(demultiplexer_1_out29), .Q(sp_Value), .clk(Clock));  // open: clr
  Register #(.width(32)) register_24 (
    .D(Write_Data), .en(demultiplexer_1_out31), .Q(ra_Value), .clk(Clock));  // open: clr
  Register #(.width(32)) register_25 (.D(Write_Data), .en(demultiplexer_1_out11), .Q(o11), .clk(Clock));  // open: clr
  Register #(.width(32)) register_26 (.D(Write_Data), .en(demultiplexer_1_out13), .Q(o13), .clk(Clock));  // open: clr
  Register #(.width(32)) register_27 (.D(Write_Data), .en(demultiplexer_1_out15), .Q(o15), .clk(Clock));  // open: clr
  Register #(.width(32)) register_28 (
    .D(Write_Data), .en(demultiplexer_1_out17), .Q(s1_Value), .clk(Clock));  // open: clr
  Register #(.width(32)) register_29 (.D(Write_Data), .en(demultiplexer_1_out19), .Q(o19), .clk(Clock));  // open: clr
  Register #(.width(32)) register_30 (.D(Write_Data), .en(demultiplexer_1_out21), .Q(o21), .clk(Clock));  // open: clr
  Register #(.width(32)) register_31 (.D(Write_Data), .en(demultiplexer_1_out23), .Q(o23), .clk(Clock));  // open: clr
  Multiplexer #(.select(5), .width(32)) multiplexer_1 (
    .in0({32{1'b0}}), .in1(o1), .in2(o2), .in3(o3), .in4(o4), .in5(o5), .in6(o6), .in7(o7), .in8(o8),
    .in9(o9), .in10(o10), .in11(o11), .in12(o12), .in13(o13), .in14(o14), .in15(o15), .in16(s0_Value),
    .in17(s1_Value), .in18(s2_Value), .in19(o19), .in20(o20), .in21(o21), .in22(o22), .in23(o23), .in24(o24),
    .in25(o25), .in26(o26), .in27(o27), .in28(o28), .in29(sp_Value), .in30(o30), .in31(ra_Value),
    .out(Read_Data_1), .sel(Read_Register_1));  // open: en
  Multiplexer #(.select(5), .width(32)) multiplexer_2 (
    .in0({32{1'b0}}), .in1(o1), .in2(o2), .in3(o3), .in4(o4), .in5(o5), .in6(o6), .in7(o7), .in8(o8),
    .in9(o9), .in10(o10), .in11(o11), .in12(o12), .in13(o13), .in14(o14), .in15(o15), .in16(s0_Value),
    .in17(s1_Value), .in18(s2_Value), .in19(o19), .in20(o20), .in21(o21), .in22(o22), .in23(o23), .in24(o24),
    .in25(o25), .in26(o26), .in27(o27), .in28(o28), .in29(sp_Value), .in30(o30), .in31(ra_Value),
    .out(Read_Data_2), .sel(Read_Register_2));  // open: en

  // Other names for the same wires on the sheet: clk = Clock; o16[31:0] = s0_Value; o17[31:0] = s1_Value;
  //   o18[31:0] = s2_Value; o29[31:0] = sp_Value; o31[31:0] = ra_Value; read_data1[31:0] = Read_Data_1;
  //   read_data2[31:0] = Read_Data_2; read_reg1[4:0] = Read_Register_1; read_reg2[4:0] = Read_Register_2;
  //   write_en = Write_Enable; write_reg[4:0] = Write_Register

  // Notes on the sheet:
  //   INPUTS to your circuit
  //   DON'T CHANGE THE LOCATIONS OF THE INPUTS AND OUTPUTS!
  //   These are DEBUG/TEST outputs from your circuit.
  //   OUTPUTS from your circuit
endmodule
